# Fritzing sketch bbw2 (saved by Fritzing 0.9.3b)

parts:
  LED1 = LED - 5mm [color="Red (633nm)" package="5 mm [THT]"]
  VCC1 = Battery
  S1 = Toggle Switch [package=THT]
  LED2 = LED - 5mm [color="Yellow (595nm)" package="5 mm [THT]"]

nets:
  N1: LED1.cathode, VCC1.+, LED2.cathode
  N2: LED1.anode, S1.L1, LED2.anode
  N3: VCC1.-, S1.COM
